// Logisim project 4_bit_ALU.circ as structural Verilog: 1 circuit, main circuit main
module main (
  input  [3:0] Number_A,
  input  [3:0] Number_B,
  input  [3:0] Number_C,
  input  [3:0] Number_D,
  input  [2:0] Selector,
  input  [3:0] Number_A_2,
  input  [3:0] Number_B_2,
  input  [2:0] Opcode,
  output [3:0] Output,
  output [3:0] Output_2
);

  wire [3:0] adder_1_out, divider_1_out, multiplier_1_out, subtractor_1_out;

  Multiplexer #(.select(3), .width(4)) multiplexer_1 (
    .in0(Number_A), .in1(Number_B), .in2(Number_C), .in3(Number_D), .out(Output), .sel(Selector));  // open: in4, in5, in6, in7, en
  Adder #(.width(4)) adder_1 (.a(Number_A_2), .b(Number_B_2), .out(adder_1_out));  // open: cin, cout
  Subtractor #(.width(4)) subtractor_1 (.a(Number_A_2), .b(Number_B_2), .out(subtractor_1_out));  // open: bin, bout
  Multiplier #(.width(4)) multiplier_1 (.a(Number_A_2), .b(Number_B_2), .out(multiplier_1_out));  // open: cin, cout
  Divider #(.width(4)) divider_1 (.a(Number_A_2), .b(Number_B_2), .out(divider_1_out));  // open: upper, rem
  Multiplexer #(.select(3), .width(4)) multiplexer_2 (
    .in0(adder_1_out), .in1(subtractor_1_out), .in2(multiplier_1_out), .in3(divider_1_out), .out(Output_2),
    .sel(Opcode));  // open: in4, in5, in6, in7, en
endmodule
